// Logisim project alu.circ as structural Verilog
module addsub (
  input  in_1,
  input  in_2,
  input  in_3,
  input  in_4,
  input  in_5,
  input  in_6,
  input  in_7,
  input  in_8,
  input  in_9,
  input  in_10,
  input  in_11,
  input  in_12,
  input  in_13,
  input  in_14,
  input  in_15,
  input  in_16,
  input  in_17,
  output out_18,
  output out_19,
  output out_20,
  output out_21,
  output out_22,
  output out_23,
  output out_24,
  output out_25,
  output out_26
);

  wire fad_2_out_5, fad_3_out_5, fad_4_out_5, fad_5_out_5, fad_6_out_5, fad_7_out_5, fad_8_out_5, xor_1_out,
       xor_2_out, xor_3_out, xor_4_out, xor_5_out, xor_6_out, xor_7_out, xor_8_out;

  xor xor_1 (xor_1_out, in_2, in_17);
  fad fad_1 (.in_2(xor_1_out), .in_3(in_1), .in_1(fad_3_out_5), .out_5(out_18), .out_4(out_19));
  xor xor_2 (xor_2_out, in_4, in_17);
  fad fad_2 (.in_2(xor_3_out), .in_3(in_5), .in_1(fad_4_out_5), .out_5(fad_2_out_5), .out_4(out_21));
  fad fad_3 (.in_2(xor_2_out), .in_3(in_3), .in_1(fad_2_out_5), .out_5(fad_3_out_5), .out_4(out_20));
  xor xor_3 (xor_3_out, in_6, in_17);
  xor xor_4 (xor_4_out, in_8, in_17);
  fad fad_4 (.in_2(xor_4_out), .in_3(in_7), .in_1(fad_5_out_5), .out_5(fad_4_out_5), .out_4(out_22));
  xor xor_5 (xor_5_out, in_10, in_17);
  fad fad_5 (.in_2(xor_5_out), .in_3(in_9), .in_1(fad_7_out_5), .out_5(fad_5_out_5), .out_4(out_23));
  xor xor_6 (xor_6_out, in_12, in_17);
  fad fad_6 (.in_2(xor_8_out), .in_3(in_13), .in_1(fad_8_out_5), .out_5(fad_6_out_5), .out_4(out_25));
  fad fad_7 (.in_2(xor_6_out), .in_3(in_11), .in_1(fad_6_out_5), .out_5(fad_7_out_5), .out_4(out_24));
  xor xor_7 (xor_7_out, in_16, in_17);
  xor xor_8 (xor_8_out, in_14, in_17);
  fad fad_8 (.in_2(xor_7_out), .in_3(in_15), .in_1(in_17), .out_5(fad_8_out_5), .out_4(out_26));
endmodule

module fad (
  input  in_1,
  input  in_2,
  input  in_3,
  output out_4,
  output out_5
);

  wire and_1_out, and_2_out, and_3_out;

  and and_1 (and_1_out, in_2, in_3);
  and and_2 (and_2_out, in_2, in_1);
  and and_3 (and_3_out, in_3, in_1);
  xor xor_1 (out_4, in_2, in_3, in_1);
  or or_1 (out_5, and_1_out, and_2_out, and_3_out);
endmodule
