// Logisim project mux.circ as structural Verilog: 5 circuits, main circuit 8muxnaif
module _8muxnaif (
  input  in_1,
  input  in_2,
  input  in_3,
  input  in_4,
  input  in_5,
  input  in_6,
  input  in_7,
  input  in_8,
  input  in_9,
  input  in_10,
  input  in_11,
  output out_12
);

  wire and_1_out, and_2_out, and_3_out, and_4_out, and_5_out, and_6_out, and_7_out, and_8_out, dec38_1_out_4,
       dec38_1_out_5, dec38_1_out_6, dec38_1_out_7, dec38_1_out_8, dec38_1_out_9, dec38_1_out_10,
       dec38_1_out_11;

  dec38 dec38_1 (
    .in_1(in_8), .in_2(in_6), .in_3(in_4), .out_4(dec38_1_out_4), .out_5(dec38_1_out_5),
    .out_6(dec38_1_out_6), .out_7(dec38_1_out_7), .out_8(dec38_1_out_8), .out_9(dec38_1_out_9),
    .out_10(dec38_1_out_10), .out_11(dec38_1_out_11));
  and and_1 (and_1_out, in_1, dec38_1_out_11);
  and and_2 (and_2_out, in_2, dec38_1_out_10);
  and and_3 (and_3_out, in_3, dec38_1_out_9);
  and and_4 (and_4_out, in_5, dec38_1_out_8);
  and and_5 (and_5_out, in_7, dec38_1_out_7);
  and and_6 (and_6_out, in_9, dec38_1_out_6);
  and and_7 (and_7_out, in_10, dec38_1_out_5);
  and and_8 (and_8_out, in_11, dec38_1_out_4);
  or or_1 (out_12, and_1_out, and_2_out, and_3_out, and_4_out, and_5_out, and_6_out, and_7_out, and_8_out);
endmodule

module _2mux (
  input  a,
  input  b,
  input  choix,
  output out_4
);

  wire and_1_out, and_2_out;

  and and_1 (and_1_out, a, choix);
  and and_2 (and_2_out, b, ~choix);  // AND_Gate
  or or_1 (out_4, and_1_out, and_2_out);
endmodule

module dec38 (
  input  in_1,
  input  in_2,
  input  in_3,
  output out_4,
  output out_5,
  output out_6,
  output out_7,
  output out_8,
  output out_9,
  output out_10,
  output out_11
);

  and and_1 (out_4, in_1, in_2, in_3);
  and and_2 (out_5, in_1, in_2, ~in_3);  // AND_Gate
  and and_3 (out_7, in_1, ~in_2, ~in_3);  // AND_Gate
  and and_4 (out_6, in_1, ~in_2, in_3);  // AND_Gate
  and and_5 (out_8, ~in_1, in_2, in_3);  // AND_Gate
  and and_6 (out_9, ~in_1, in_2, ~in_3);  // AND_Gate
  and and_7 (out_10, ~in_1, ~in_2, in_3);  // AND_Gate
  and and_8 (out_11, ~in_1, ~in_2, ~in_3);  // AND_Gate
endmodule

module _4mux (
  input  a3,
  input  a2,
  input  a1,
  input  a0,
  input  c0,
  input  c1,
  output out_7
);

  wire n2mux_1_out_4, n2mux_3_out_4;

  _2mux u_2mux_1 (.a(a3), .b(a2), .choix(c0), .out_4(n2mux_1_out_4));
  _2mux u_2mux_2 (.a(n2mux_1_out_4), .b(n2mux_3_out_4), .choix(c1), .out_4(out_7));
  _2mux u_2mux_3 (.a(a1), .b(a0), .choix(c0), .out_4(n2mux_3_out_4));
endmodule

module _8mux (
  input  in_1,
  input  in_2,
  input  in_3,
  input  in_4,
  input  in_5,
  input  in_6,
  input  in_7,
  input  in_8,
  input  in_9,
  input  in_10,
  input  in_11,
  output out_12
);

  wire n4mux_1_out_7, n4mux_2_out_7;

  _4mux u_4mux_1 (.a3(in_1), .a2(in_2), .a1(in_3), .a0(in_4), .c0(in_11), .c1(in_10), .out_7(n4mux_1_out_7));
  _2mux u_2mux_1 (.a(n4mux_1_out_7), .b(n4mux_2_out_7), .choix(in_9), .out_4(out_12));
  _4mux u_4mux_2 (.a3(in_5), .a2(in_6), .a1(in_7), .a0(in_8), .c0(in_11), .c1(in_10), .out_7(n4mux_2_out_7));
endmodule
