// Logisim project tp2.circ as structural Verilog: 3 circuits, main circuit main
module main (
);

  wire button_1_out, flip_flop_1_out_3, flip_flop_2_out_3, flip_flop_3_out_3, flip_flop_4_out_3,
       flip_flop_5_out_3, flip_flop_6_out_3, not_1_out, or_1_out;

  or or_1 (or_1_out, flip_flop_6_out_3, ~flip_flop_1_out_3);  // OR_Gate
  flip_flop flip_flop_1 (.in_1(button_1_out), .in_2(1'b0), .out_3(flip_flop_1_out_3));
  LED led_1 (.in(or_1_out));
  flip_flop flip_flop_2 (.in_1(or_1_out), .in_2(not_1_out), .out_3(flip_flop_2_out_3));
  not not_1 (not_1_out, button_1_out);
  Button button_1 (.out(button_1_out));
  LED led_2 (.in(flip_flop_2_out_3));
  flip_flop flip_flop_3 (.in_1(flip_flop_2_out_3), .in_2(not_1_out), .out_3(flip_flop_3_out_3));
  LED led_3 (.in(flip_flop_3_out_3));
  LED led_4 (.in(flip_flop_4_out_3));
  flip_flop flip_flop_4 (.in_1(flip_flop_3_out_3), .in_2(not_1_out), .out_3(flip_flop_4_out_3));
  LED led_5 (.in(flip_flop_5_out_3));
  flip_flop flip_flop_5 (.in_1(flip_flop_4_out_3), .in_2(not_1_out), .out_3(flip_flop_5_out_3));
  flip_flop flip_flop_6 (.in_1(flip_flop_5_out_3), .in_2(not_1_out), .out_3(flip_flop_6_out_3));
endmodule

module latch (
  input  ck,
  input  e,
  output out_3
);

  Multiplexer multiplexer_1 (.in0(e), .in1(out_3), .out(out_3), .sel(ck));  // open: en
endmodule

// ck
module flip_flop (
  input  in_1,
  input  in_2,
  output out_3
);

  wire and_1_out, clock_1_out, latch_1_out_3, not_1_out;

  Clock clock_1 (.out(clock_1_out));
  latch latch_1 (.e(and_1_out), .ck(clock_1_out), .out_3(latch_1_out_3));
  and and_1 (and_1_out, in_1, ~in_2);  // AND_Gate
  not not_1 (not_1_out, clock_1_out);
  latch latch_2 (.e(latch_1_out_3), .ck(not_1_out), .out_3(out_3));
endmodule
