// Logisim project tp3.circ as structural Verilog: 6 circuits, main circuit main
module main (
  input  reboot,
  output [1:0] out_2
);

  wire clock_1_out, register_2_q;
  wire [1:0] adder_1_out;

  Adder #(.width(2)) adder_1 (.a(out_2), .b(2'b01), .out(adder_1_out));  // open: cin, cout
  Register #(.width(2)) register_1 (.D(adder_1_out), .Q(out_2), .clk(clock_1_out), .clr(register_2_q));  // open: en
  Clock clock_1 (.out(clock_1_out));
  Register #(.width(1)) register_2 (.D(reboot), .Q(register_2_q), .clk(clock_1_out));  // open: en, clr
endmodule

module fib (
  input  in_1
);

  wire clock_1_out;
  wire [15:0] adder_1_out, multiplexer_1_out, multiplexer_2_out, register_1_q, register_2_q;

  Multiplexer #(.width(16)) multiplexer_1 (
    .in0({16{1'b0}}), .in1(register_2_q), .out(multiplexer_1_out), .sel(in_1));  // open: en
  Multiplexer #(.width(16)) multiplexer_2 (
    .in0(16'h1), .in1(adder_1_out), .out(multiplexer_2_out), .sel(in_1));  // open: en
  Register #(.width(16)) register_1 (.D(multiplexer_1_out), .Q(register_1_q), .clk(clock_1_out));  // open: en, clr
  Register #(.width(16)) register_2 (.D(multiplexer_2_out), .Q(register_2_q), .clk(clock_1_out));  // open: en, clr
  Clock clock_1 (.out(clock_1_out));
  Adder #(.width(16)) adder_1 (.a(register_1_q), .b(register_2_q), .out(adder_1_out));  // open: cin, cout
endmodule

module rappelT (
  input  in_1,
  input  [2:0] in_2,
  output [2:0] out_3
);


  assign out_3 = {in_2[1:0], in_1};
endmodule

module rappelF (
  input  [2:0] in_1,
  output out_2
);

  and and_1 (out_2, in_1[0], in_1[1], in_1[2]);
endmodule

module rappel (
  input  in_1,
  input  in_2,
  output out_3
);

  wire clock_1_out, undriven;
  wire [2:0] rappelt_1_out_3, register_1_q;

  rappelT rappelt_1 (.in_2(register_1_q), .in_1(in_1), .out_3(rappelt_1_out_3));
  Register #(.width(3)) register_1 (
    .D(rappelt_1_out_3), .en(undriven), .Q(register_1_q), .clk(clock_1_out), .clr(in_2));
  Clock clock_1 (.out(clock_1_out));
  rappelF rappelf_1 (.in_1(register_1_q), .out_2(out_3));
endmodule

module multT (
  input  [15:0] a,
  input  [7:0] b,
  input  [15:0] c
);

  wire [7:0] and_1_out;

  assign and_1_out = 8'h1 & b;  // AND_Gate and_1, 8 bits wide
endmodule
